// Logisim project adder.circ as structural Verilog: 2 circuits, main circuit main
module main (
  input  [15:0] B,
  input  [15:0] A,
  input  sub,
  output [15:0] result,
  output ovf
);

  wire adding1bit_1_cout, adding1bit_2_cout, adding1bit_3_cout, adding1bit_4_cout, adding1bit_5_cout,
       adding1bit_6_cout, adding1bit_7_cout, adding1bit_8_cout, adding1bit_9_cout, adding1bit_10_cout,
       adding1bit_11_cout, adding1bit_12_cout, adding1bit_13_cout, adding1bit_14_cout, adding1bit_15_cout,
       adding1bit_16_cout, xor_2_out, xor_3_out, xor_4_out, xor_5_out, xor_6_out, xor_7_out, xor_8_out,
       xor_9_out, xor_10_out, xor_11_out, xor_12_out, xor_13_out, xor_14_out, xor_15_out, xor_16_out,
       xor_17_out;

  xor xor_1 (ovf, adding1bit_1_cout, adding1bit_2_cout);
  Adding1Bit adding1bit_1 (
    .A(xor_2_out), .B(A[15]), .Cin(adding1bit_2_cout), .Cout(adding1bit_1_cout), .Sum(result[15]));
  xor xor_2 (xor_2_out, sub, B[15]);
  Adding1Bit adding1bit_2 (
    .A(xor_3_out), .B(A[14]), .Cin(adding1bit_3_cout), .Cout(adding1bit_2_cout), .Sum(result[14]));
  xor xor_3 (xor_3_out, sub, B[14]);
  Adding1Bit adding1bit_3 (
    .A(xor_4_out), .B(A[13]), .Cin(adding1bit_4_cout), .Cout(adding1bit_3_cout), .Sum(result[13]));
  xor xor_4 (xor_4_out, sub, B[13]);
  Adding1Bit adding1bit_4 (
    .A(xor_5_out), .B(A[12]), .Cin(adding1bit_5_cout), .Cout(adding1bit_4_cout), .Sum(result[12]));
  xor xor_5 (xor_5_out, sub, B[12]);
  Adding1Bit adding1bit_5 (
    .A(xor_7_out), .B(A[11]), .Cin(adding1bit_7_cout), .Cout(adding1bit_5_cout), .Sum(result[11]));
  xor xor_6 (xor_6_out, sub, B[10]);
  xor xor_7 (xor_7_out, sub, B[11]);
  Adding1Bit adding1bit_6 (.A(xor_8_out), .B(A[9]), .Cin(adding1bit_8_cout), .Cout(adding1bit_6_cout), .Sum(result[9]));
  Adding1Bit adding1bit_7 (
    .A(xor_6_out), .B(A[10]), .Cin(adding1bit_6_cout), .Cout(adding1bit_7_cout), .Sum(result[10]));
  xor xor_8 (xor_8_out, sub, B[9]);
  Adding1Bit adding1bit_8 (.A(xor_9_out), .B(A[8]), .Cin(adding1bit_9_cout), .Cout(adding1bit_8_cout), .Sum(result[8]));
  xor xor_9 (xor_9_out, sub, B[8]);
  Adding1Bit adding1bit_9 (
    .A(xor_10_out), .B(A[7]), .Cin(adding1bit_10_cout), .Cout(adding1bit_9_cout), .Sum(result[7]));
  xor xor_10 (xor_10_out, sub, B[7]);
  Adding1Bit adding1bit_10 (
    .A(xor_11_out), .B(A[6]), .Cin(adding1bit_11_cout), .Cout(adding1bit_10_cout), .Sum(result[6]));
  xor xor_11 (xor_11_out, sub, B[6]);
  Adding1Bit adding1bit_11 (
    .A(xor_12_out), .B(A[5]), .Cin(adding1bit_12_cout), .Cout(adding1bit_11_cout), .Sum(result[5]));
  xor xor_12 (xor_12_out, sub, B[5]);
  Adding1Bit adding1bit_12 (
    .A(xor_13_out), .B(A[4]), .Cin(adding1bit_13_cout), .Cout(adding1bit_12_cout), .Sum(result[4]));
  xor xor_13 (xor_13_out, sub, B[4]);
  Adding1Bit adding1bit_13 (
    .A(xor_14_out), .B(A[3]), .Cin(adding1bit_15_cout), .Cout(adding1bit_13_cout), .Sum(result[3]));
  xor xor_14 (xor_14_out, sub, B[3]);
  xor xor_15 (xor_15_out, sub, B[2]);
  Adding1Bit adding1bit_14 (
    .A(xor_16_out), .B(A[1]), .Cin(adding1bit_16_cout), .Cout(adding1bit_14_cout), .Sum(result[1]));
  Adding1Bit adding1bit_15 (
    .A(xor_15_out), .B(A[2]), .Cin(adding1bit_14_cout), .Cout(adding1bit_15_cout), .Sum(result[2]));
  xor xor_16 (xor_16_out, sub, B[1]);
  Adding1Bit adding1bit_16 (.A(xor_17_out), .B(A[0]), .Cin(sub), .Cout(adding1bit_16_cout), .Sum(result[0]));
  xor xor_17 (xor_17_out, sub, B[0]);

  // Other names for the same wires on the sheet: a00 = A[0]; a01 = A[1]; a02 = A[2]; a03 = A[3]; a04 = A[4];
  //   a05 = A[5]; a06 = A[6]; a07 = A[7]; a08 = A[8]; a09 = A[9]; b00 = B[0]; b01 = B[1]; b02 = B[2]; b03 = B[3];
  //   b04 = B[4]; b05 = B[5]; b06 = B[6]; b07 = B[7]; b08 = B[8]; b09 = B[9]
endmodule

module Adding1Bit (
  input  A,
  input  B,
  input  Cin,
  output Cout,
  output Sum
);

  wire and_1_out, and_2_out, xor_1_out;

  and and_1 (and_1_out, A, B);
  xor xor_1 (xor_1_out, A, B);
  and and_2 (and_2_out, xor_1_out, Cin);
  or or_1 (Cout, and_1_out, and_2_out);
  xor xor_2 (Sum, xor_1_out, Cin);
endmodule
