// Logisim project circuit1c.circ as structural Verilog: 1 circuit, main circuit main
module main (
  input  A,
  input  B,
  input  C,
  output out1,
  output out2
);

  wire and_1_out, and_2_out, and_3_out, and_4_out, OA, OB, OC;

  not not_1 (OA, A);
  not not_2 (OB, B);
  not not_3 (OC, C);
  and and_1 (and_1_out, OA, C);
  and and_2 (and_2_out, A, B);
  and and_3 (and_3_out, OA, OB, OC);
  and and_4 (and_4_out, A, OC);
  or or_1 (out1, and_4_out, and_1_out, B);
  or or_2 (out2, and_2_out, and_3_out);

  // Other names for the same wires on the sheet: SA = A; SB = B; SC = C
endmodule
